# Fritzing sketch Projeto (saved by Fritzing 0.9.6b)
breadboards: 2

parts:
  Part1 = NRF24L01+ Breakout Board
  BAT1 = BC9VPC [package=bc9vpc]
  S1 = Pushbutton [package="[THT]"]
  S2 = Pushbutton [package="[THT]"]
  Part2 = Arduino Uno (Rev3) - ICSP
  R1 = Resistor [tolerance=±5% resistance=220 package="2010 [SMD]"]
  R2 = Resistor [tolerance=±5% resistance=220 package="2010 [SMD]"]
  LED1 = LED - 5mm [color="Red (633nm)" current=0.030 package="5 mm [THT]"]
  ANT1 = Antenna  # not connected
  Part5 = Arduino Uno (Rev3) - ICSP
  Part6 = NRF24L01+ Breakout Board
  R3 = Resistor [tolerance=±5% resistance=220 package="2010 [SMD]"]
  ANT3 = Antenna  # not connected
  BAT2 = BC9VPC [package=bc9vpc]  # not connected
  BAT3 = BC9VPC [package=bc9vpc]  # not connected
  C5 = Ceramic Capacitor [capacitance=0.1µF voltage=35V package="200 mil [THT, multilayer]"]
  C6 = Ceramic Capacitor [capacitance=1µF voltage=35V package="200 mil [THT, multilayer]"]
  U2 = Voltage Regulator [package=to220-adj]
  R4 = Resistor [tolerance=±10% resistance=470 part_number=R2 package="1206 [SMD]"]
  R5 = Resistor [tolerance=±5% resistance=330 part_number=R1 package="1206 [SMD]"]

nets:
  N1: Part1.GND, BAT1.V-, C5.0, R4.Pin_0
  N2: Part1.VCC, C6.1, U2.IN, U2.OUT, R4.Pin_1, R5.Pin_0, R5.Pin_1
  N3: Part1.CE, Part2.D9_PWM
  N4: Part1.CS, Part2.D10_PWM/SS
  N5: Part1.SCK, Part2.D13/SCK
  N6: Part1.MOSI, Part2.D11_PWM/MOSI
  N7: Part1.MISO, Part2.D12/MISO
  N8: BAT1.V+, C5.1, C6.0, U2.ADJ
  N9: S1.Pin_1, S1.Pin_2, S2.Pin_1, S2.Pin_2, Part2.5V
  N10: S1.Pin_3, S1.Pin_4, Part2.D5_PWM, R2.Pin_0
  N11: S2.Pin_3, S2.Pin_4, Part2.D4, R1.Pin_0
  N12: Part2.GND, R2.Pin_1
  GND: LED1.cathode, Part5.GND, Part6.GND
  N13: LED1.anode, R3.Pin_0
  N14: Part5.D9_PWM, Part6.CE
  N15: Part5.D10_PWM/SS, Part6.CS
  N16: Part5.D11_PWM/MOSI, Part6.MOSI
  N17: Part5.D12/MISO, Part6.MISO
  N18: Part5.D13/SCK, Part6.SCK
  N19: Part5.D4, R3.Pin_1
  3V3: Part5.3V3, Part6.VCC

notes:
  VO = 1.25V (1+ R2/ R1) + Iadj R2
